// Logisim project CIRCUITO DIAGRAMA SOMA DE PRODUTOS.circ as structural Verilog
module SoP (
  input  A,
  input  B,
  input  C,
  input  D,
  output OUT2,
  output OUT1,
  output OUT0
);

  wire and_1_out, and_2_out, and_3_out, and_4_out, and_5_out, and_6_out, and_7_out, and_8_out, and_9_out,
       and_10_out, and_11_out, and_12_out, not_1_out, not_2_out, not_3_out, not_4_out, not_5_out, not_6_out,
       not_7_out, not_8_out, not_9_out, not_10_out, not_11_out, not_12_out, not_13_out, not_14_out,
       not_15_out, not_16_out, not_17_out, not_18_out, not_19_out, or_3_out;

  not not_1 (not_1_out, A);
  not not_2 (not_2_out, B);
  and and_1 (and_1_out, not_1_out, not_2_out, D);
  not not_3 (not_3_out, A);
  and and_2 (and_2_out, not_3_out, not_4_out, D);
  not not_4 (not_4_out, C);
  and and_3 (and_3_out, A, not_5_out, not_6_out);
  not not_5 (not_5_out, B);
  not not_6 (not_6_out, D);
  and and_4 (and_4_out, A, not_7_out, not_8_out);
  not not_7 (not_7_out, C);
  not not_8 (not_8_out, D);
  and and_5 (and_5_out, A, B, C, D);
  not not_9 (not_9_out, A);
  and and_6 (and_6_out, not_9_out, not_10_out, C);
  not not_10 (not_10_out, B);
  not not_11 (not_11_out, A);
  and and_7 (and_7_out, not_11_out, C, not_12_out);
  not not_12 (not_12_out, D);
  not not_13 (not_13_out, B);
  and and_8 (and_8_out, not_13_out, C, not_14_out);
  not not_14 (not_14_out, D);
  and and_9 (and_9_out, A, not_15_out, D);
  not not_15 (not_15_out, C);
  not not_16 (not_16_out, A);
  not not_17 (not_17_out, D);
  not not_18 (not_18_out, C);
  not not_19 (not_19_out, B);
  and and_10 (and_10_out, not_16_out, B, not_17_out);
  and and_11 (and_11_out, B, not_18_out);
  and and_12 (and_12_out, A, not_19_out, C, D);
  or or_1 (OUT2, and_12_out, and_11_out, and_10_out);
  or or_2 (OUT1, and_9_out, and_8_out, and_7_out, and_6_out);
  or or_3 (or_3_out, and_5_out, and_4_out, and_3_out, and_2_out, and_1_out);
endmodule
